# Fritzing sketch 1LED (saved by Fritzing 0.9.2b)
breadboards: 1

parts:
  Raspberry_Pi_1 = Raspberry Pi 3 [part_number=RPI-3-V1.2]
  LED1 = smd LED [color="Red (633nm)" package="0805 [SMD]"]
  R1 = Resistor [tolerance=±5% resistance=220 package="1206 [SMD]"]

nets:
  N1: Raspberry_Pi_1.GIPO18, LED1.anode
  N2: Raspberry_Pi_1.GND, R1.Pin_1
  N3: LED1.cathode, R1.Pin_0

notes:
  @PIR4T3

// code stored in the sketch: Untitled.ino
import RPi.GPIO as GPIO
import time
GPIO.setmode(GPIO.BCM)
GPIO.setwarnings(False)
GPIO.setup(18,GPIO.OUT)
print "LED on"
GPIO.output(18,GPIO.HIGH)
time.sleep(3)
print "LED off"
GPIO.output(18,GPIO.LOW)


#!/usr/bin/env python
import RPi.GPIO as GPIO
import time

RelayPin = 11    # pin11

def setup():
	GPIO.setmode(GPIO.BOARD)       # Numbers GPIOs by physical location
	GPIO.setup(RelayPin, GPIO.OUT)
	GPIO.output(RelayPin, GPIO.HIGH)

def loop():
	while True:
		print '...relayd on'
		GPIO.output(RelayPin, GPIO.LOW)
		time.sleep(0.5)
		print 'relay off...'
		GPIO.output(RelayPin, GPIO.HIGH)
		time.sleep(0.5)

def destroy():
	GPIO.output(RelayPin, GPIO.HIGH)
	GPIO.cleanup()                     # Release resource

if __name__ == '__main__':     # Program start from here
	setup()
	try:
		loop()
	except KeyboardInterrupt:  # When 'Ctrl+C' is pressed, the child program destroy() will be  executed.
		destroy()
