# Fritzing sketch RELAY (saved by Fritzing 0.9.3b)
breadboards: 1

parts:
  KY-1 = Keyes Relay [package=THT]
  Raspberry_Pi_1 = Raspberry Pi 3 [part_number=RPI-3-V1.2]
  HLK-PM1 = HLK-PM01
  LED1 = LED - 5mm [color="Red (633nm)" package="5 mm [THT]"]

nets:
  N1: KY-1.signal, Raspberry_Pi_1.5V
  N2: KY-1.power, Raspberry_Pi_1.GIPO18
  N3: KY-1.ground, Raspberry_Pi_1.GND
  N4: KY-1.NC, LED1.cathode
  N5: KY-1.C, HLK-PM1.AC#1
  N6: HLK-PM1.AC#0, LED1.anode

notes:
  100W Bulb
  @PIR4T3

custom parts:
  Keyes Relay: The Keyes 5V relay module is suitable for SCM development, home appliance control. It uses a 5V~12V TIL control signal which can control DC / AC signal.
